# Fritzing sketch line following robot (saved by Fritzing 0.9.3b)
breadboards: 1

parts:
  Part1 = Arduino Uno (Rev3)
  Part2 = Motor Driver 1A Dual TB6612FNG  # not connected
  R1 = PHOTOCELL [package=photocell]
  R2 = Resistor [tolerance=±5% resistance=220 package="0402 [SMD]"]
  R3 = PHOTOCELL [package=photocell]
  R4 = Resistor [tolerance=±5% resistance=220 package="0402 [SMD]"]

nets:
  N1: Part1.A0, R3.P$1, R4.Pin_1
  N2: Part1.A1, R1.P$1, R2.Pin_1
  N3: Part1.GND, R2.Pin_0, R4.Pin_0
  N4: Part1.5V, R1.P$2, R3.P$2
