# Fritzing sketch line following robot (saved by Fritzing 0.9.3b)
breadboards: 1

parts:
  Part1 = Arduino Uno (Rev3)
  R1 = PHOTOCELL [package=photocell]
  R2 = Resistor [tolerance=±5% resistance=220 package="0402 [SMD]"]
  R3 = PHOTOCELL [package=photocell]
  R4 = Resistor [tolerance=±5% resistance=220 package="0402 [SMD]"]
  Part3 = Adafruit TB6612 DC and Stepper Motor Driver [part_number="Adafruit #2448"]
  M1 = DC Motor
  M2 = DC Motor
  VCC1 = Battery
  R5 = Resistor [tolerance=±5% resistance=220 package=THT]
  LED1 = LED - 5mm [color="Red (633nm)" package="5 mm [THT]"]
  R6 = Resistor [tolerance=±5% resistance=220 package=THT]
  LED2 = LED - 5mm [color="Red (633nm)" package="5 mm [THT]"]
  R7 = Resistor [tolerance=±5% resistance=220 package=THT]
  LED3 = LED - 5mm [color="Red (633nm)" package="5 mm [THT]"]

nets:
  N1: Part1.A0, R1.P$1, R2.Pin_1
  N2: Part1.A1, R3.P$1, R4.Pin_1
  N3: Part1.D8, R7.Pin_1
  N4: Part1.D10_PWM/SS, Part3.PWMA
  N5: Part1.D11_PWM/MOSI, Part3.PWMB
  GND: Part1.GND, R2.Pin_0, R4.Pin_0, Part3.GND, VCC1.-, LED1.anode, LED2.anode, LED3.anode
  N6: Part1.D4, Part3.AIN2
  N7: Part1.D5_PWM, Part3.AIN1
  N8: Part1.D6_PWM, Part3.BIN1
  N9: Part1.D7, Part3.BIN2
  5V: Part1.5V, R1.P$2, R3.P$2, Part3.VCC, R5.Pin_1, R6.Pin_1
  N10: Part3.PWRIN, VCC1.+
  N11: Part3.MOTORA1, M1.pin_2
  N12: Part3.MOTORA2, M1.pin_1
  N13: Part3.MOTORB2, M2.pin_2
  N14: Part3.MOTORB1, M2.pin_1
  N15: R5.Pin_0, LED1.cathode
  N16: R6.Pin_0, LED2.cathode
  N17: R7.Pin_0, LED3.cathode

custom parts:
  Adafruit TB6612 DC and Stepper Motor Driver: Spin two DC motors, step one bi-polar or uni-polar stepper, or fire off two solenoids with 1.2A per channel using the TB6612. These are perhaps better known as "the drivers in our assembled Adafruit Motorshield or Motor HAT." We really like these dual H-bridges, so if you want to control motors without a shield or HAT these are easy to include on any solderless breadboard or perma-proto.
